// Logisim project F3-2to4-decoder.circ as structural Verilog: 3 circuits, main circuit main
module main (
  input  in_1,
  input  in_2,
  input  in_3,
  output out_4,
  output out_5,
  output out_6,
  output out_7,
  output out_8,
  output out_9,
  output out_10,
  output out_11
);

  wire transistor_1_out;

  Transistor transistor_1 (.in(1'b1), .out(transistor_1_out), .gate(in_3));
  Transistor #(.\type ("n")) transistor_2 (.in(1'b0), .out(transistor_1_out), .gate(in_3));
  decoder24 decoder24_1 (._1(in_1), ._2(in_2), .en(transistor_1_out), .Y0(out_4), .Y1(out_5), .Y2(out_6), .Y3(out_7));
  decoder24 decoder24_2 (._1(in_1), ._2(in_2), .en(in_3), .Y0(out_8), .Y1(out_9), .Y2(out_10), .Y3(out_11));
endmodule

module OR2 (
  input  A,
  input  B,
  output Y
);

  wire transistor_1_out, transistor_2_out;

  Transistor transistor_1 (.in(1'b1), .out(transistor_1_out), .gate(A));
  Transistor transistor_2 (.in(transistor_1_out), .out(transistor_2_out), .gate(B));
  Transistor #(.\type ("n")) transistor_3 (.in(1'b0), .out(transistor_2_out), .gate(A));
  Transistor #(.\type ("n")) transistor_4 (.in(1'b0), .out(transistor_2_out), .gate(B));
  Transistor transistor_5 (.in(1'b1), .out(Y), .gate(transistor_2_out));
  Transistor #(.\type ("n")) transistor_6 (.in(1'b0), .out(Y), .gate(transistor_2_out));
endmodule

module decoder24 (
  input  _1,
  input  _2,
  input  en,
  output Y0,
  output Y1,
  output Y2,
  output Y3
);

  wire transistor_1_out, transistor_3_out, transistor_5_out, transistor_6_out, transistor_7_out,
       transistor_8_out, transistor_11_out, transistor_12_out, transistor_15_out, transistor_16_out,
       transistor_19_out, transistor_20_out, transistor_21_out, transistor_26_out;

  Transistor transistor_1 (.in(1'b1), .out(transistor_1_out), .gate(_1));
  Transistor #(.\type ("n")) transistor_2 (.in(1'b0), .out(transistor_1_out), .gate(_1));
  Transistor transistor_3 (.in(1'b1), .out(transistor_3_out), .gate(_2));
  Transistor #(.\type ("n")) transistor_4 (.in(1'b0), .out(transistor_3_out), .gate(_2));
  Transistor transistor_5 (.in(1'b1), .out(transistor_5_out), .gate(transistor_1_out));
  Transistor transistor_6 (.in(1'b1), .out(transistor_6_out), .gate(_1));
  Transistor #(.\type ("n")) transistor_7 (.in(1'b0), .out(transistor_7_out), .gate(en));
  Transistor #(.\type ("n")) transistor_8 (.in(transistor_7_out), .out(transistor_8_out), .gate(transistor_1_out));
  Transistor #(.\type ("n")) transistor_9 (.in(transistor_8_out), .out(transistor_5_out), .gate(transistor_3_out));
  Transistor transistor_10 (.in(1'b1), .out(transistor_5_out), .gate(en));
  Transistor #(.\type ("n")) transistor_11 (.in(1'b0), .out(transistor_11_out), .gate(en));
  Transistor #(.\type ("n")) transistor_12 (.in(transistor_11_out), .out(transistor_12_out), .gate(_1));
  Transistor #(.\type ("n")) transistor_13 (.in(transistor_12_out), .out(transistor_6_out), .gate(transistor_3_out));
  Transistor transistor_14 (.in(1'b1), .out(transistor_6_out), .gate(en));
  Transistor #(.\type ("n")) transistor_15 (.in(transistor_26_out), .out(transistor_15_out), .gate(transistor_1_out));
  Transistor #(.\type ("n")) transistor_16 (.in(transistor_15_out), .out(transistor_16_out), .gate(_2));
  Transistor transistor_17 (.in(1'b1), .out(transistor_16_out), .gate(en));
  Transistor transistor_18 (.in(1'b1), .out(transistor_16_out), .gate(transistor_1_out));
  Transistor #(.\type ("n")) transistor_19 (.in(1'b0), .out(transistor_19_out), .gate(en));
  Transistor #(.\type ("n")) transistor_20 (.in(transistor_19_out), .out(transistor_20_out), .gate(_1));
  Transistor #(.\type ("n")) transistor_21 (.in(transistor_20_out), .out(transistor_21_out), .gate(_2));
  Transistor transistor_22 (.in(1'b1), .out(transistor_21_out), .gate(en));
  Transistor transistor_23 (.in(1'b1), .out(transistor_21_out), .gate(_1));
  Transistor transistor_24 (.in(1'b1), .out(transistor_5_out), .gate(transistor_3_out));
  Transistor transistor_25 (.in(1'b1), .out(transistor_6_out), .gate(transistor_3_out));
  Transistor #(.\type ("n")) transistor_26 (.in(1'b0), .out(transistor_26_out), .gate(en));
  Transistor transistor_27 (.in(1'b1), .out(transistor_16_out), .gate(_2));
  Transistor transistor_28 (.in(1'b1), .out(transistor_21_out), .gate(_2));
  Transistor transistor_29 (.in(1'b1), .out(Y0), .gate(transistor_5_out));
  Transistor #(.\type ("n")) transistor_30 (.in(1'b0), .out(Y0), .gate(transistor_5_out));
  Transistor transistor_31 (.in(1'b1), .out(Y1), .gate(transistor_6_out));
  Transistor #(.\type ("n")) transistor_32 (.in(1'b0), .out(Y1), .gate(transistor_6_out));
  Transistor transistor_33 (.in(1'b1), .out(Y2), .gate(transistor_16_out));
  Transistor #(.\type ("n")) transistor_34 (.in(1'b0), .out(Y2), .gate(transistor_16_out));
  Transistor transistor_35 (.in(1'b1), .out(Y3), .gate(transistor_21_out));
  Transistor #(.\type ("n")) transistor_36 (.in(1'b0), .out(Y3), .gate(transistor_21_out));
endmodule
